# Fritzing sketch CIRC01 (saved by Fritzing 0.9.2b)
circuit board: 1.82108cm x 1.5389cm
breadboards: 1

parts:
  LED = LEDs [package=led10mm]
  resistor = Resistor [tolerance=±5% resistance=560 package=THT]
  Part1 = Arduino Uno (Rev3)
  V1 = DC Power [voltage=5]
  Pad3 = Pad [width=3 height=3 connect=center]
  Pad4 = Pad [width=3 height=3 connect=center]
  Header1 = 2 pin header [package=THT]
  Header2 = 2 pin header [package=THT]
  Header3 = 2 pin header [package=THT]
  Header4 = 2 pin header [package=THT]

nets:
  N1: LED.C, resistor.Pin_0
  pin 13: LED.A, Part1.D13/SCK, Pad3.pad
  GND: resistor.Pin_1, Part1.GND, V1.V-, Pad4.pad, Header1.pin_1#1, Header2.pin_1#1
  5V: Part1.5V, V1.V+, Header1.pin_1#0, Header2.pin_1#0
  N2: Header3.pin_1#0, Header4.pin_1#0
  N3: Header3.pin_1#1, Header4.pin_1#1

notes:
  (green-blue-brown)
  Arduino
  (light emitting diode)
  (ground) (-)
  longer lead
  anode
  cathode
  longer
  lead
  10mm
  LED

custom parts:
  2 pin header: 2 pin male to male header
