# Fritzing sketch CIRC02 (saved by Fritzing 0.9.2b)
circuit board: 6.44199cm x 1.82025cm
breadboards: 1

parts:
  R1 = Resistor [tolerance=±5% resistance=560 package=THT]
  R7 = Resistor [tolerance=±5% resistance=560 package=THT]
  R6 = Resistor [tolerance=±5% resistance=560 package=THT]
  R5 = Resistor [tolerance=±5% resistance=560 package=THT]
  R4 = Resistor [tolerance=±5% resistance=560 package=THT]
  R3 = Resistor [tolerance=±5% resistance=560 package=THT]
  R2 = Resistor [tolerance=±5% resistance=560 package=THT]
  R8 = Resistor [tolerance=±5% resistance=560 package=THT]
  Part1 = Arduino Uno (Rev3)
  Pad1 = Pad [width=3 height=3 connect=center]
  Pad2 = Pad [width=3 height=3 connect=center]
  Pad3 = Pad [width=3 height=3 connect=center]
  Pad4 = Pad [width=3 height=3 connect=center]
  Pad5 = Pad [width=3 height=3 connect=center]
  Pad6 = Pad [width=3 height=3 connect=center]
  Pad7 = Pad [width=3 height=3 connect=center]
  Pad8 = Pad [width=3 height=3 connect=center]
  Pad9 = Pad [width=3 height=3 connect=center]
  LED1 = LED - 5mm [color="Green (560nm)" package="5 mm [THT]"]
  LED2 = LED - 5mm [color="Green (560nm)" package="5 mm [THT]"]
  LED3 = LED - 5mm [color="Green (560nm)" package="5 mm [THT]"]
  LED4 = LED - 5mm [color="Green (560nm)" package="5 mm [THT]"]
  LED5 = LED - 5mm [color="Green (560nm)" package="5 mm [THT]"]
  LED6 = LED - 5mm [color="Green (560nm)" package="5 mm [THT]"]
  LED7 = LED - 5mm [color="Green (560nm)" package="5 mm [THT]"]
  LED8 = LED - 5mm [color="Green (560nm)" package="5 mm [THT]"]
  Header1 = 2 pin header [package=THT]
  Header2 = 2 pin header [package=THT]
  Header3 = 2 pin header [package=THT]
  Header4 = 2 pin header [package=THT]

nets:
  GND: R1.Pin_0, R7.Pin_0, R6.Pin_0, R5.Pin_0, R4.Pin_0, R3.Pin_0, R2.Pin_0, R8.Pin_0, Part1.GND, Pad9.pad, Header3.pin_1#1, Header4.pin_1#1
  N1: R1.Pin_1, LED1.cathode
  N2: R7.Pin_1, LED7.cathode
  N3: R6.Pin_1, LED6.cathode
  N4: R5.Pin_1, LED5.cathode
  N5: R4.Pin_1, LED4.cathode
  N6: R3.Pin_1, LED3.cathode
  N7: R2.Pin_1, LED2.cathode
  N8: R8.Pin_1, LED8.cathode
  pin 8: Part1.D8, Pad7.pad, LED7.anode
  pin 9: Part1.D9_PWM, Pad8.pad, LED8.anode
  pin 2: Part1.D2, Pad1.pad, LED1.anode
  pin 3: Part1.D3_PWM, Pad2.pad, LED2.anode
  pin 4: Part1.D4, Pad3.pad, LED3.anode
  pin 5: Part1.D5_PWM, Pad4.pad, LED4.anode
  pin 6: Part1.D6_PWM, Pad5.pad, LED5.anode
  pin 7: Part1.D7, Pad6.pad, LED6.anode
  5V: Part1.5V, Header3.pin_1#0, Header4.pin_1#0
  N9: Header1.pin_1#0, Header2.pin_1#0
  N10: Header1.pin_1#1, Header2.pin_1#1

notes:
  longer
  lead
  5mm
  LED
  to 5V
  to Gnd

custom parts:
  2 pin header: 2 pin male to male header
