# Fritzing sketch CIRC03 (saved by Fritzing 0.9.2b)
circuit board: 1.70143cm x 1.27329cm
breadboards: 1

parts:
  Part1 = Arduino Uno (Rev3)
  resistor = Resistor [tolerance=±5% resistance=2.2k package=THT]
  Diode = Rectifier Diode [part_number=1N4001 package="300 mil [THT]"]
  Transistor = NPN-Transistor [part_number=P2N2222AG package="TO92 [THT]"]
  C1 = Electrolytic Capacitor [capacitance=0.22mF voltage=16V package="100 mil [THT, electrolytic]"]
  Pad1 = Pad [width=2.04 height=2.04 connect=center]
  Pad3 = Pad [width=2.04 height=2.04 connect=center]
  Pad4 = Pad [width=2.04 height=2.04 connect=center]  # not connected
  Pad5 = Pad [width=2.04 height=2.04 connect=center]  # not connected
  Pad6 = Pad [width=2.04 height=2.04 connect=center]
  Motor = DC Motor
  Pad2 = Pad [width=2.04 height=2.04 connect=center]  # not connected
  Header1 = 2 pin header [package=THT]
  Header2 = 2 pin header [package=THT]
  Header3 = 2 pin header [package=THT]
  Header4 = 2 pin header [package=THT]

nets:
  pin 9: Part1.D9_PWM, resistor.Pin_1, Pad6.pad
  GND: Part1.GND, Transistor.E, C1.-, Pad1.pad, Header3.pin_1#1, Header4.pin_1#1
  5V: Part1.5V, Diode.cathode, C1.+, Pad3.pad, Motor.pin_1, Header3.pin_1#0, Header4.pin_1#0
  N1: resistor.Pin_0, Transistor.B
  N2: Diode.anode, Transistor.C, Motor.pin_2
  N3: Header1.pin_1#0, Header2.pin_1#0
  N4: Header1.pin_1#1, Header2.pin_1#1

notes:
  Transistor
  (P2N2222A)
  2.2Kohm
  optional
  Capacitor
  220µF
  longer
  lead
  diode
  (ground) (-)
  Collector
  Base
  Emitter
  Arduino
  E
  C
  B

custom parts:
  2 pin header: 2 pin male to male header
