# Fritzing sketch CIRC04 (saved by Fritzing 0.9.2b)
circuit board: 1.07369cm x 1.30005cm
breadboards: 1

parts:
  Part1 = Arduino Uno (Rev3)
  Mini_Servo = Basic Servo
  Pad1 = Pad [width=2.04 height=2.04 connect=center]
  Pad2 = Pad [width=2.04 height=2.04 connect=center]
  Pad3 = Pad [width=2.04 height=2.04 connect=center]

nets:
  pin 9: Part1.D9_PWM, Mini_Servo.pulse, Pad1.pad
  5V: Part1.5V, Mini_Servo.vcc, Pad2.pad
  GND: Part1.GND, Mini_Servo.gnd, Pad3.pad

notes:
  (ground) (-)
  gnd
  (black or brown)
  (red)
  +5v
  signal
  (white, yellow, or orange)
  Arduino
