# Fritzing sketch CIRC06 (saved by Fritzing 0.9.2b)
circuit board: 0.842513cm x 1.01411cm
breadboards: 1

parts:
  Piezo = Piezo Speaker
  Part1 = Arduino Uno (Rev3)
  Pad1 = Pad [width=2.04 height=2.04 connect=center]
  Pad2 = Pad [width=2.04 height=2.04 connect=center]

nets:
  pin 9: Piezo.pin1, Part1.D9_PWM, Pad2.pad
  GND: Piezo.pin2, Part1.GND, Pad1.pad
  5V: Part1.5V

notes:
  (ground) (-)
  Arduino
  Element
  Piezo
