# Fritzing sketch CIRC07 (saved by Fritzing 0.9.2b)
circuit board: 1.72063cm x 2.46099cm
breadboards: 1

parts:
  Part1 = Arduino Uno (Rev3)
  R2 = Resistor [tolerance=±5% resistance=10k package=THT]
  R1 = Resistor [tolerance=±5% resistance=560 package=THT]
  LED = LED - 5mm [color="Red (633nm)" package="5 mm [THT]"]
  Pushbutton = Pushbutton [package="[THT]"]
  S2 = Pushbutton [package="[THT]"]
  R3 = Resistor [tolerance=±5% resistance=10k package=THT]
  Pad1 = Pad [width=2.04 height=2.04 connect=center]
  Pad3 = Pad [width=2.04 height=2.04 connect=center]
  Pad4 = Pad [width=2.04 height=2.04 connect=center]
  Pad5 = Pad [width=2.04 height=2.04 connect=center]
  Pad2 = Pad [width=2.04 height=2.04 connect=center]

nets:
  pin 13: Part1.D13/SCK, LED.anode, Pad2.pad
  GND: Part1.GND, R1.Pin_1, Pushbutton.Pin_3, Pushbutton.Pin_4, S2.Pin_3, S2.Pin_4, Pad5.pad
  pin 2: Part1.D2, R2.Pin_0, S2.Pin_1, S2.Pin_2, Pad4.pad
  pin 3: Part1.D3_PWM, Pushbutton.Pin_1, Pushbutton.Pin_2, R3.Pin_0, Pad3.pad
  5V: Part1.5V, R2.Pin_1, R3.Pin_1, Pad1.pad
  N1: R1.Pin_0, LED.cathode

notes:
  Arduino
  longer
  lead
  Push
  button
  S1
  on
  off
  (ground) (-)
