# Fritzing sketch CIRC09 (saved by Fritzing 0.9.2b)
circuit board: 2.34126cm x 1.34946cm
breadboards: 1

parts:
  Part1 = Arduino Uno (Rev3)
  photo = Photocell (LDR) [package=THT]
  R1 = Resistor [tolerance=±5% resistance=560 package=THT]
  R2 = Resistor [tolerance=±5% resistance=10k package=THT]
  LED = LED - 5mm [color="Green (560nm)" package="5 mm [THT]"]
  Pad1 = Pad [width=3.0864372907029587 height=1.4532792539684496 connect=center]
  Pad4 = Pad [width=3.0864372907029587 height=1.4532792539684496 connect=center]
  Pad3 = Pad [width=3.0864372907029587 height=1.4532792539684496 connect=center]
  Pad2 = Pad [width=3.0864372907029587 height=1.4532792539684496 connect=center]

nets:
  pin 0: Part1.A0, photo.pin_1, R2.Pin_1, Pad2.pad
  pin 9: Part1.D9_PWM, LED.anode, Pad3.pad
  GND: Part1.GND, R1.Pin_1, R2.Pin_0, Pad4.pad
  5V: Part1.5V, photo.pin_0, Pad1.pad
  N1: R1.Pin_0, LED.cathode

notes:
  (ground) (-)
  analog
  Arduino
  resistor
  LDR
  Photo
  Resistor
  longer
  lead
  10k
  ohm
