# Fritzing sketch CIRC11hb (saved by Fritzing 0.9.2b)
circuit board: 1.895cm x 2.71801cm
breadboards: 1

parts:
  Part1 = Arduino Uno (Rev3)
  R1 = Resistor [tolerance=±5% resistance=2.2k package=THT]
  Diode = Rectifier Diode [part_number=1N4001 package="300 mil [THT]"]
  Pad3 = Pad [width=3 height=3 connect=center]
  Pad2 = Pad [width=3 height=3 connect=center]
  Pad1 = Pad [width=3 height=3 connect=center]
  Motor = DC Motor
  Relay1_3 = 941 Series Relay [package=THT]
  Relay1_1 = 941 Series Relay [package=THT]
  Relay1 = 941 Series Relay [package=THT]
  Relay1_2 = 941 Series Relay [package=THT]
  Transistor = NPN-Transistor [part_number=2N2222AG package="TO92 [THT]"]

nets:
  GND: Part1.GND, Pad1.pad, Relay1_3.Switch_2_Normally_Open, Relay1.connector5, Relay1.connector8, Relay1_2.Switch_1_Normally_Closed, Transistor.E
  pin 2: Part1.D2, R1.Pin_1, Pad2.pad
  5V: Part1.5V, Diode.cathode, Pad3.pad, Relay1_3.Switch_2_Normally_Closed, Relay1_1.Coil_2, Relay1.connector7, Relay1.connector10, Relay1.connector15, Relay1_2.Switch_1_Normally_Open
  N1: R1.Pin_0, Transistor.B
  N2: Diode.anode, Relay1_1.Coil_1, Relay1.connector0, Transistor.C
  N3: Motor.pin_1, Relay1_3.Switch_2_Common, Relay1.connector12
  N4: Motor.pin_2, Relay1.connector3, Relay1_2.Switch_1_Common

notes:
  Emitter
  Collector
  Base
  (flyback)
  diode
  2.2k
  ohm
  DPDT
  relay
  Transistor
  P2N2222A
  coil
  com
  NC
  NO
  -
  +
  to 5V
  to Gnd
  (ground) (-)

custom parts:
  941 Series Relay: DPDT Dual in-line relay
  941 Series Relay: DPDT Dual in-line relay
  941 Series Relay: DPDT Dual in-line relay
  941 Series Relay: DPDT Dual in-line relay
