# Fritzing sketch CIRC15 (saved by Fritzing 0.9.2b)
circuit board: 5.56468cm x 1.81232cm
breadboards: 1

parts:
  LED2 = LED - 5mm [color="Red (633nm)" package="5 mm [THT]"]
  LED3 = LED - 5mm [color="Red (633nm)" package="5 mm [THT]"]
  LED4 = LED - 5mm [color="Red (633nm)" package="5 mm [THT]"]
  LED5 = LED - 5mm [color="Red (633nm)" package="5 mm [THT]"]
  LED6 = LED - 5mm [color="Red (633nm)" package="5 mm [THT]"]
  Part1 = Arduino Uno (Rev3)
  LED1 = LED - 5mm [color="Red (633nm)" package="5 mm [THT]"]
  V1 = DC Power [voltage=5]
  R6 = Resistor [tolerance=±5% resistance=560 package=THT]
  R1 = Resistor [tolerance=±5% resistance=560 package=THT]
  R2 = Resistor [tolerance=±5% resistance=560 package=THT]
  R3 = Resistor [tolerance=±5% resistance=560 package=THT]
  R4 = Resistor [tolerance=±5% resistance=560 package=THT]
  R5 = Resistor [tolerance=±5% resistance=560 package=THT]
  S1 = Momentary Switch [package=ksa_sealed_tac_switch]
  R7 = Resistor [tolerance=±1% resistance=2.2k package=THT]

nets (from the schematic view):
  N1: LED2.cathode, Part1.D3_PWM
  N2: LED2.anode, R2.Pin_1
  N3: LED3.cathode, Part1.D4
  N4: LED3.anode, R3.Pin_1
  N5: LED4.cathode, Part1.D5_PWM
  N6: LED4.anode, R4.Pin_1
  N7: LED5.cathode, Part1.D6_PWM
  N8: LED5.anode, R5.Pin_1
  N9: LED6.cathode, Part1.D7
  N10: LED6.anode, R6.Pin_1
  N11: Part1.D12/MISO, R7.Pin_1
  GND: Part1.GND, V1.V-, R6.Pin_0, R1.Pin_0, R2.Pin_0, R3.Pin_0, R4.Pin_0, R5.Pin_0, S1.3
  N12: Part1.D2, LED1.cathode
  5V: Part1.5V, V1.V+
  N13: LED1.anode, R1.Pin_1
  N14: S1.1, R7.Pin_0
